// Logisim project 7.减法器7.circ as structural Verilog: 1 circuit, main circuit main
module main (
  input  A0,
  input  in_2,
  input  in_3,
  input  A3,
  input  B0,
  input  in_6,
  input  in_7,
  input  B3,
  input  S
);

  wire adder_1_cout, adder_2_cout, adder_3_cout, adder_4_cout, not_1_out, not_2_out;
  wire [3:0] adder_1_out, xor_4_out, xor_5_out;

  xor xor_1 (xor_4_out[3], B3, S);
  xor xor_2 (xor_4_out[2], in_7, S);
  xor xor_3 (xor_4_out[1], in_6, S);
  xor xor_4 (xor_4_out[0], B0, S);
  Adder #(.width(4)) adder_1 (.a({A3, in_3, in_2, A0}), .b(xor_4_out), .out(adder_1_out), .cin(S), .cout(adder_1_cout));
  Adder #(.width(4)) adder_2 (
    .a({A3, in_3, in_2, A0}), .b(xor_4_out), .out(adder_1_out), .cin(adder_1_cout), .cout(adder_2_cout));
  Adder #(.width(4)) adder_3 (
    .a({A3, in_3, in_2, A0}), .b(xor_4_out), .out(adder_1_out), .cin(adder_2_cout), .cout(adder_3_cout));
  Adder #(.width(4)) adder_4 (
    .a({A3, in_3, in_2, A0}), .b(xor_4_out), .out(adder_1_out), .cin(adder_3_cout), .cout(adder_4_cout));
  not not_1 (not_1_out, adder_4_cout);
  LED led_1 (.in(not_1_out));
  _7_Segment_Display u_7_segment_display_1 (
    .g(1'b1), .b(not_2_out), .c(not_2_out), .dp(not_2_out));  // open: f, a, e, d
  Hex_Digit_Display hex_digit_display_1 (.value({A3, in_3, in_2, A0}));  // open: dp
  assign xor_5_out = xor_4_out ^ {4{S}};  // XOR_Gate xor_5, 4 bits wide
  not not_2 (not_2_out, S);
  _7_Segment_Display u_7_segment_display_2 (.g(S), .d(S));  // open: f, a, b, e, c, dp
  Hex_Digit_Display hex_digit_display_2 (.value(xor_5_out));  // open: dp
  Hex_Digit_Display hex_digit_display_3 (.value(adder_1_out));  // open: dp

  // Notes on the sheet:
  //   异或的奇妙用法，取反
  //   4个小加加分线器合成一个大加法器
  //   ＝
  //   一
  //   减法器，再来一个异的
  //   相当于可以控制的4非
  //   要明白取反相当于减法号
  //   原码减法减一
  //   与异与或前面加一个异
  //   减一法
endmodule
